// Logisim project calc_medie.circ as structural Verilog
module main (
  input  in_1,
  input  in_2,
  input  [2:0] in_3,
  input  [2:0] in_4,
  output [7:0] out_5,
  output [7:0] out_6
);

  gen_nr_mx gen_nr_mx_1 (.clk(in_1), .reset(in_2), .sel(in_3), .O(out_5));
  medii_RAM_ROM medii_ram_rom_1 (.sel(in_4), .O(out_6));
endmodule

// VHDL entity shift_medie, as the project stores it:
--------------------------------------------------------------------------------
-- Project :
-- File    :
-- Autor   :
-- Date    :
--
--------------------------------------------------------------------------------
-- Description :
--
--------------------------------------------------------------------------------

LIBRARY ieee;
USE ieee.std_logic_1164.all;
use ieee.numeric_std.all;
use IEEE.STD_LOGIC_UNSIGNED.ALL;

ENTITY shift_medie IS
  PORT (	suma: in std_logic_vector(7 downto 0);
  		sel: in std_logic_vector(2 downto 0);
  		clk: in std_logic;
  		media: out std_logic_vector(7 downto 0)
  );
END shift_medie;

--------------------------------------------------------------------------------
--Complete your VHDL description below
--------------------------------------------------------------------------------

ARCHITECTURE arch_shift_medie OF shift_medie IS

BEGIN
process(sel, suma, clk)
begin
	if(rising_edge(clk)) then 
		if(sel = "000") then 
			media <= "00000000";
		end if;
		
		if(sel = "100") then
			media <= "0" & suma(7 downto 1);
		end if;

		if(sel = "101") then
			media <= "00" & suma(7 downto 2);
		end if;

		if(sel = "110") then 
			media <= "000" & suma(7 downto 3);
		end if;

		if(sel = "111") then
			media <= "0000" & suma(7 downto 4);
		end if;
	end if;
end process;

END arch_shift_medie;

// VHDL entity MUX, as the project stores it:
LIBRARY ieee;
USE ieee.std_logic_1164.all;
entity MUX is
	port(I1, I2: in std_logic_vector(7 downto 0);
		sel: in std_logic_vector(2 downto 0);
		O: out std_logic_vector(7 downto 0)
	);
end MUX;

architecture arch_MUX of MUX is
signal O_aux: std_logic_vector(7 downto 0);
begin
	process(sel,I1,I2)
	begin
		if(sel = "110") then
			O_aux <= I1;

		elsif(sel = "111") then
			O_aux <= I2;
		else O_aux <= "00000000";
		end if;

	end process;
	O <= O_aux;
end arch_MUX;

// VHDL entity gen_nr_pseudo, as the project stores it:
LIBRARY ieee;
USE ieee.std_logic_1164.all;

USE ieee.numeric_std.all;
ENTITY gen_nr_pseudo IS
  PORT (
  	clk: in std_logic;
  	sel: in std_logic_vector(2 downto 0);
  	ies1: out std_logic_vector(7 downto 0);
  	ies2: out std_logic_vector(7 downto 0)
    );
END gen_nr_pseudo;


ARCHITECTURE arch_gen_nr_pseudo OF gen_nr_pseudo IS

BEGIN
	
	process(clk)
	
	variable ies_aux_1: std_logic_vector(7 downto 0) :="00001111";
	variable ies_aux_2: std_logic_vector(7 downto 0):="11111111";
	variable s1: std_logic;
	variable s2: std_logic;
	
	begin
	s1:=ies_aux_1(3) xor ies_aux_1(0);
	s2:=ies_aux_2(7) xor ies_aux_2(0);
	
	if(sel = "110") then 
		s1 :=ies_aux_1(3) xor ies_aux_1(0);
		if(rising_edge(clk)) then
			ies_aux_1 :="0000" & ies_aux_1(2 downto 0) & s1;
		end if;
	
		ies1 <= ies_aux_1;
		ies2 <= "00000000";
	end if;

	if(sel = "111") then 
		s2 :=ies_aux_2(7) xor ies_aux_2(0);
		if(rising_edge(clk)) then
			ies_aux_2 := ies_aux_2(6 downto 0) & s2;
		end if;

		ies1 <= "00001111";
		ies2 <= ies_aux_2;
	end if;
	end process;

END arch_gen_nr_pseudo;

// VHDL entity gen_nr_mx, as the project stores it:
LIBRARY ieee;
USE ieee.std_logic_1164.all;
USE ieee.numeric_std.all;
ENTITY gen_nr_mx is
	PORT(
	clk,reset: in std_logic;
	sel: in std_logic_vector(2 downto 0);
	O:out std_logic_vector(7 downto 0)
	);
end gen_nr_mx;

architecture ARH of gen_nr_mx is

	component MX is
	port(I1, I2: in std_logic_vector(7 downto 0);
		sel: in std_logic_vector(2 downto 0);
		O: out std_logic_vector(7 downto 0)
		);
	end component;

	component gen_nr is
	PORT(clk: in std_logic;
  		sel: in std_logic_vector(2 downto 0);
  		ies1: out std_logic_vector(7 downto 0);
  		ies2: out std_logic_vector(7 downto 0)
    	);
   	end component;

	signal i1, i2: std_logic_vector(7 downto 0);
	
	begin
	pas1: gen_nr port map(clk, sel, i1, i2);
	pas2: MX port map(i1, i2, sel, O);
	
end architecture ARH;



LIBRARY ieee;
USE ieee.std_logic_1164.all;
USE ieee.numeric_std.all;
ENTITY gen_nr IS
  PORT(
  	clk: in std_logic;
  	sel: in std_logic_vector(2 downto 0);
  	ies1: out std_logic_vector(7 downto 0);
  	ies2: out std_logic_vector(7 downto 0)
    );
END gen_nr;


ARCHITECTURE arch_gen_nr OF gen_nr IS
BEGIN
	process(clk)
	
	variable ies_aux_1: std_logic_vector(7 downto 0) :="00001111";
	variable ies_aux_2: std_logic_vector(7 downto 0):="11111111";
	variable s1: std_logic;
	variable s2: std_logic;
	
	begin

	s1:=ies_aux_1(3) xor ies_aux_1(0);
	s2:=ies_aux_2(7) xor ies_aux_2(0);
	
	if(sel = "110") then 
		s1 :=ies_aux_1(3) xor ies_aux_1(0);
		if(rising_edge(clk)) then
			ies_aux_1 :="0000" & ies_aux_1(2 downto 0) & s1;
		end if;
	
		ies1 <= ies_aux_1;
		ies2 <= "00000000";
	end if;

	if(sel = "111") then 
		s2 :=ies_aux_2(7) xor ies_aux_2(0);
		if(rising_edge(clk)) then
			ies_aux_2 := ies_aux_2(6 downto 0) & s2;
		end if;

		ies1 <= "00001111";
		ies2 <= ies_aux_2;
	end if;
	end process;

END arch_gen_nr;


LIBRARY ieee;
USE ieee.std_logic_1164.all;
entity MX is
	port(I1, I2: in std_logic_vector(7 downto 0);
		sel: in std_logic_vector(2 downto 0);
		O: out std_logic_vector(7 downto 0)
	);
end MX;

architecture arch_MUX of MX is
signal O_aux: std_logic_vector(7 downto 0);
begin
	process(sel,I1,I2)
	begin
		if(sel = "110") then
			O_aux <= I1;

		elsif(sel = "111") then
			O_aux <= I2;
		else O_aux <= "00000000";
		end if;

	end process;
	O <= O_aux;
end arch_MUX;

// VHDL entity medii_RAM_ROM, as the project stores it:
LIBRARY ieee;
USE ieee.std_logic_1164.all;
USE ieee.std_logic_unsigned.all;
USE ieee.std_logic_arith.all;
use ieee.numeric_std.all;
ENTITY medii_RAM_ROM IS
  PORT (sel: in std_logic_vector(2 downto 0);
  	   O: out std_logic_vector(7 downto 0)
  );
END medii_RAM_ROM;

ARCHITECTURE arch_medii_RAM_ROM OF medii_RAM_ROM IS
	type MATRICE is array (0 to 5) of std_logic_vector(7 downto 0);
BEGIN
	process(sel)

		variable mem_1: MATRICE := ("00110110","10100100","10100010","01011011","01101000","00010101");
		variable mem_2: MATRICE := ("11001001","01011011","01011101","10100100","10010111","11101010");
		variable sum: natural;
		
	begin
		if(sel = "010") then
			sum:=0;
			for i in 0 to 5 loop
				sum := sum + conv_integer(mem_1(i));
			end loop;
			sum := sum / 6;
		end if;

		if(sel ="011") then
			sum:=0;
			for i in 0 to 5 loop
				sum := sum + conv_integer(mem_2(i));
			end loop;
			sum := sum / 6;
		end if;

		O <= std_logic_vector(TO_UNSIGNED(sum, 8));
		
	end process;
	

END arch_medii_RAM_ROM;
